// Logisim project Absolute.circ as structural Verilog: 1 circuit, main circuit Absolute
module Absolute (
  input  [27:0] A,
  output [26:0] Y
);

  wire [26:0] _1_s_Comp, bit_extender_1_out;

  // _7486 7486_1: pin names not known; wires that end beside it: A[27], A[12], _1_s_Comp[12], A[27], A[13], _1_s_Comp[13], A[27], A[15], _1_s_Comp[15], A[27], A[14], _1_s_Comp[14]
  // _7486 7486_2: pin names not known; wires that end beside it: A[27], A[24], _1_s_Comp[24], A[27], A[25], _1_s_Comp[25], A[27], A[26], _1_s_Comp[26]
  // _7486 7486_3: pin names not known; wires that end beside it: A[27], A[0], _1_s_Comp[0], A[27], A[1], _1_s_Comp[1], A[27], A[3], _1_s_Comp[3], A[27], A[2], _1_s_Comp[2]
  // _7486 7486_4: pin names not known; wires that end beside it: A[27], A[4], _1_s_Comp[4], A[27], A[5], _1_s_Comp[5], A[27], A[7], _1_s_Comp[7], A[27], A[6], _1_s_Comp[6]
  // _7486 7486_5: pin names not known; wires that end beside it: A[27], A[16], _1_s_Comp[16], A[27], A[17], _1_s_Comp[17], A[27], A[19], _1_s_Comp[19], A[27], A[18], _1_s_Comp[18]
  assign bit_extender_1_out = {{26{1'b0}}, 1'b0};  // Bit_Extender bit_extender_1
  Adder #(.width(27)) adder_1 (.a(_1_s_Comp), .b(bit_extender_1_out), .out(Y), .cin(A[27]));  // open: cout
  // _7486 7486_6: pin names not known; wires that end beside it: A[27], A[8], _1_s_Comp[8], A[27], A[9], _1_s_Comp[9], A[27], A[11], _1_s_Comp[11], A[27], A[10], _1_s_Comp[10]
  // _7486 7486_7: pin names not known; wires that end beside it: A[27], A[20], _1_s_Comp[20], A[27], A[21], _1_s_Comp[21], A[27], A[23], _1_s_Comp[23], A[27], A[22], _1_s_Comp[22]

  // Other names for the same wires on the sheet: Y0 = _1_s_Comp[0]; Y1 = _1_s_Comp[1]; Y2 = _1_s_Comp[2];
  //   Y3 = _1_s_Comp[3]; Y4 = _1_s_Comp[4]; Y5 = _1_s_Comp[5]; Y6 = _1_s_Comp[6]; Y7 = _1_s_Comp[7];
  //   Y8 = _1_s_Comp[8]; Y9 = _1_s_Comp[9]; Y10 = _1_s_Comp[10]; Y11 = _1_s_Comp[11]; Y12 = _1_s_Comp[12];
  //   Y13 = _1_s_Comp[13]; Y14 = _1_s_Comp[14]; Y15 = _1_s_Comp[15]; Y16 = _1_s_Comp[16]; Y17 = _1_s_Comp[17];
  //   Y18 = _1_s_Comp[18]; Y19 = _1_s_Comp[19]; Y20 = _1_s_Comp[20]; Y21 = _1_s_Comp[21]; Y22 = _1_s_Comp[22];
  //   Y23 = _1_s_Comp[23]; Y24 = _1_s_Comp[24]; Y25 = _1_s_Comp[25]; Y26 = _1_s_Comp[26]; Sign = A[27]
endmodule
