// Logisim project Add_Sub.circ as structural Verilog: 1 circuit, main circuit Add/Sub
module Add_Sub (
  input  in_1,
  input  Add,
  input  [26:0] A,
  input  [26:0] B,
  output [27:0] Y
);

  wire adder_1_cout, subtractor_1_bout;
  wire [26:0] adder_1_out, subtractor_1_out;

  Adder #(.width(27)) adder_1 (.a(A), .b(B), .out(adder_1_out), .cin(in_1), .cout(adder_1_cout));
  Subtractor #(.width(27)) subtractor_1 (.a(A), .b(B), .out(subtractor_1_out), .bin(in_1), .bout(subtractor_1_bout));
  Multiplexer #(.enable("false")) multiplexer_1 (.in0(subtractor_1_bout), .in1(adder_1_cout), .out(Y[27]), .sel(Add));
  Multiplexer #(.width(27), .enable("false")) multiplexer_2 (
    .in0(subtractor_1_out), .in1(adder_1_out), .out(Y[26:0]), .sel(Add));

  // Other names for the same wires on the sheet: B_in_C_in = in_1
endmodule
