// Logisim project FPA.circ as structural Verilog: 17 circuits, main circuit FloatingPointAdder
module main (
  input  [31:0] A,
  input  [31:0] B,
  output [31:0] Y,
  output out_4,
  output out_5,
  output Infinity,
  output Not_a_Number,
  output Denormalized_Number
);

  wire Large0or1, Large_sign, NormalizingOverflow, RoundingOverflow, SameSign, Sign_A, Sign_B, Small_sign;
  wire [8:0] Expo_A, Expo_B, Exponent_Shift, Large_Expo, NormalExponent, Small_Expo;
  wire [21:0] Fraction_A, Fraction_B, Large_Fraction;
  wire [24:0] NormalSignificand;
  wire [25:0] n26_bit_mux_1_y, n26_bit_mux_2_y, Padded_Num_2;
  wire [25:3] Padded_Unshifted_Num_2;
  wire [26:0] AbsSignificand, Input1, Input2;
  wire [27:0] AddSubOutput;
  wire [31:0] Large, Small;

  _32_bit_spliter Spliter (.Input(A), .Fraction(Fraction_A), .Exponent(Expo_A), .Sign(Sign_A));
  _32_bit_spliter Spliter_2 (.Input(B), .Fraction(Fraction_B), .Exponent(Expo_B), .Sign(Sign_B));
  _32_bit_spliter Spliter_3 (.Input(Large), .Fraction(Large_Fraction), .Exponent(Large_Expo), .Sign(Large_sign));
  _32_bit_spliter Spliter_4 (
    .Input(Small), .Fraction(Padded_Unshifted_Num_2[24:3]), .Exponent(Small_Expo), .Sign(Small_sign));
  Check_If_Zero Check_Zero (.X(Large), .Zero_or_One(Large0or1));
  Check_If_Zero Check_Zero_2 (.X(Small), .Zero_or_One(Padded_Unshifted_Num_2[25]));
  xnor xnor_1 (SameSign, Sign_A, Sign_B);
  Shift_wrapper Shift_Wrapper (
    .Padded_Number({Padded_Unshifted_Num_2, 3'b000}), .Expo_difference(Exponent_Shift),
    .Shifted_Num_2(Padded_Num_2));
  // Probe on NormalSignificand
  normalizer normalizer (
    .significand(AbsSignificand), .Exponent(Large_Expo), .Normal_Fraction(NormalSignificand),
    .Normal_Exponent(NormalExponent), .Overflow(NormalizingOverflow), .Underflow(out_5));
  // Probe on {Large0or1, Large_Fraction, 3'b000}
  Rounder rounder_1 (
    .Input(NormalSignificand), .Exponent(NormalExponent), .Rounded_Fraction(Y[21:0]),
    .Rounded_Exponent(Y[30:22]), .Exponent_Overflow_While_Rounding(RoundingOverflow));
  _26_Bit_MUX u_26_bit_mux_1 (
    .B(Padded_Num_2), .Y(n26_bit_mux_1_y), .A({Large0or1, Large_Fraction, 3'b000}), .S(Large_sign));
  _26_Bit_MUX u_26_bit_mux_2 (
    .B({Large0or1, Large_Fraction, 3'b000}), .Y(n26_bit_mux_2_y), .A(Padded_Num_2), .S(Large_sign));
  Add_Sub add_sub_1 (.in_1(1'b0), .A(Input1), .B(Input2), .Add(SameSign), .Y(AddSubOutput));
  Rearrange2 rearrange (.Expo_A(Expo_A), .Expo_B(Expo_B), .A(A), .B(B), .larger(Large), .smaller(Small));
  // Probe on AddSubOutput
  // Probe on n26_bit_mux_1_y
  // Probe on n26_bit_mux_2_y
  Absolute absolute_1 (.A(AddSubOutput), .Y(AbsSignificand));
  // Probe on Input1
  assign Input1 = {{1{1'b0}}, n26_bit_mux_1_y};  // Bit_Extender bit_extender_1
  // Probe on Input2
  assign Input2 = {{1{1'b0}}, n26_bit_mux_2_y};  // Bit_Extender bit_extender_2
  // Probe on AbsSignificand
  Subtractor #(.width(9)) subtractor_1 (.a(Large_Expo), .b(Small_Expo), .out(Exponent_Shift));  // open: bin, bout
  or or_1 (out_4, NormalizingOverflow, RoundingOverflow);
  Multiplexer #(.enable("false")) multiplexer_1 (.in0(AddSubOutput[26]), .in1(Sign_A), .out(Y[31]), .sel(SameSign));
  flags Flags (
    .Normal_Exponent(NormalExponent), .Normal_Fraction(NormalSignificand), .INF(Infinity),
    .NAN(Not_a_Number), .Denormalized_Number(Denormalized_Number));

  // Other names for the same wires on the sheet: SumSIgn = AddSubOutput[26]; Overflow = out_4;
  //   Padded_Num_1[25:3] = {Large0or1, Large_Fraction}; Small_Fraction[21:0] = Padded_Unshifted_Num_2[24:3];
  //   Small0or1 = Padded_Unshifted_Num_2[25]; Underflow = out_5; RoundedSignificand[21:0] = Y[21:0];
  //   RoundedExponent[8:0] = Y[30:22]; Sign = Y[31]

  // Notes on the sheet:
  //   Rearrange:
  //   Split the larger and small number
  //   Checking if any number is Zero
  //   Padding(1.....000)
  //   Shifting the number 2
  //   How many Bits to shift
endmodule

module _1Bit_Right_Shifter (
  input  [25:0] in_1,
  input  Enable,
  output [25:0] _1Bit_RightShifted,
  output [25:0] _1_Bit_Shifted_or_not
);

  wire [27:0] bit_extender_1_out, bit_extender_2_out;
  wire [27:26] _28_bit_Mux_y;

  assign bit_extender_1_out = {{2{1'b0}}, _1Bit_RightShifted};  // Bit_Extender bit_extender_1
  assign bit_extender_2_out = {{2{1'b0}}, in_1};  // Bit_Extender bit_extender_2
  Shifter #(.width(26), .shift("lr")) shifter_1 (.in(in_1), .\dist (5'b00001), .out(_1Bit_RightShifted));
  _28_Bit_Mux _28_bit_Mux (
    .B(bit_extender_1_out), .A(bit_extender_2_out), .S(Enable), .Y({_28_bit_Mux_y, _1_Bit_Shifted_or_not}));

  // Other names for the same wires on the sheet: Shifted[25:0] = _1Bit_RightShifted; X[25:0] = in_1
endmodule

module _2Bit_Right_Shifter (
  input  [25:0] in_1,
  input  Enable,
  output [25:0] _2Bit_RightShifted,
  output [25:0] _2_Bit_Shifted_or_not
);

  wire [27:0] bit_extender_1_out, bit_extender_2_out;
  wire [27:26] _28_bit_Mux_y;

  assign bit_extender_1_out = {{2{1'b0}}, _2Bit_RightShifted};  // Bit_Extender bit_extender_1
  assign bit_extender_2_out = {{2{1'b0}}, in_1};  // Bit_Extender bit_extender_2
  Shifter #(.width(26), .shift("lr")) shifter_1 (.in(in_1), .\dist (5'b00010), .out(_2Bit_RightShifted));
  _28_Bit_Mux _28_bit_Mux (
    .B(bit_extender_1_out), .A(bit_extender_2_out), .S(Enable), .Y({_28_bit_Mux_y, _2_Bit_Shifted_or_not}));

  // Other names for the same wires on the sheet: Shifted[25:0] = _2Bit_RightShifted; X[25:0] = in_1
endmodule

module _4Bit_Right_Shifter (
  input  [25:0] in_1,
  input  Enable,
  output [25:0] _4Bit_RightShifted,
  output [25:0] _4_Bit_Shifted_or_not
);

  wire [27:0] bit_extender_1_out, bit_extender_2_out;
  wire [27:26] _28_bit_Mux_y;

  assign bit_extender_1_out = {{2{1'b0}}, _4Bit_RightShifted};  // Bit_Extender bit_extender_1
  assign bit_extender_2_out = {{2{1'b0}}, in_1};  // Bit_Extender bit_extender_2
  Shifter #(.width(26), .shift("lr")) shifter_1 (.in(in_1), .\dist (5'b00100), .out(_4Bit_RightShifted));
  _28_Bit_Mux _28_bit_Mux (
    .B(bit_extender_1_out), .A(bit_extender_2_out), .S(Enable), .Y({_28_bit_Mux_y, _4_Bit_Shifted_or_not}));

  // Other names for the same wires on the sheet: Shifted[25:0] = _4Bit_RightShifted; X[25:0] = in_1
endmodule

module _8Bit_Right_Shifter (
  input  [25:0] in_1,
  input  Enable,
  output [25:0] _8Bit_RightShifted,
  output [25:0] _8_Bit_Shifted_or_not
);

  wire [27:0] bit_extender_1_out, bit_extender_2_out;
  wire [27:26] _28_bit_Mux_y;

  assign bit_extender_1_out = {{2{1'b0}}, _8Bit_RightShifted};  // Bit_Extender bit_extender_1
  assign bit_extender_2_out = {{2{1'b0}}, in_1};  // Bit_Extender bit_extender_2
  Shifter #(.width(26), .shift("lr")) shifter_1 (.in(in_1), .\dist (5'b01000), .out(_8Bit_RightShifted));
  _28_Bit_Mux _28_bit_Mux (
    .B(bit_extender_1_out), .A(bit_extender_2_out), .S(Enable), .Y({_28_bit_Mux_y, _8_Bit_Shifted_or_not}));

  // Other names for the same wires on the sheet: Shifted[25:0] = _8Bit_RightShifted; X[25:0] = in_1
endmodule

module _16Bit_Right_Shifter (
  input  [25:0] in_1,
  input  Enable,
  output [25:0] _4Bit_RightShifted,
  output [25:0] _4_Bit_Shifted_or_not
);

  wire [27:0] bit_extender_1_out, bit_extender_2_out;
  wire [27:26] _28_bit_Mux_y;

  assign bit_extender_1_out = {{2{1'b0}}, _4Bit_RightShifted};  // Bit_Extender bit_extender_1
  assign bit_extender_2_out = {{2{1'b0}}, in_1};  // Bit_Extender bit_extender_2
  Shifter #(.width(26), .shift("lr")) shifter_1 (.in(in_1), .\dist (5'b10000), .out(_4Bit_RightShifted));
  _28_Bit_Mux _28_bit_Mux (
    .B(bit_extender_1_out), .A(bit_extender_2_out), .S(Enable), .Y({_28_bit_Mux_y, _4_Bit_Shifted_or_not}));

  // Other names for the same wires on the sheet: Shifted[25:0] = _4Bit_RightShifted; X[25:0] = in_1
endmodule

module _32_bit_spliter (
  input  [31:0] Input,
  output [21:0] Fraction,
  output [8:0] Exponent,
  output Sign
);


  assign Exponent = Input[30:22];
  assign Fraction = Input[21:0];
  assign Sign = Input[31];
endmodule

module _28_Bit_Mux (
  input  [27:0] B,
  input  [27:0] A,
  input  S,
  output [27:0] Y
);

  // _74157 74157_1: pin names not known; wires that end beside it: S, A[0], B[0], Y[0], A[1], B[1], Y[1], 1'b0, A[3], B[3], Y[3], A[2], B[2], Y[2]
  // _74157 74157_2: pin names not known; wires that end beside it: S, A[4], B[4], Y[4], A[5], B[5], Y[5], 1'b0, A[7], B[7], Y[7], A[6], B[6], Y[6]
  // _74157 74157_3: pin names not known; wires that end beside it: S, A[8], B[8], Y[8], A[9], B[9], Y[9], 1'b0, A[11], B[11], Y[11], A[10], B[10], Y[10]
  // _74157 74157_4: pin names not known; wires that end beside it: S, A[12], B[12], Y[12], A[13], B[13], Y[13], 1'b0, A[15], B[15], Y[15], A[14], B[14], Y[14]
  // _74157 74157_5: pin names not known; wires that end beside it: S, A[16], B[16], Y[16], A[17], B[17], Y[17], 1'b0, A[19], B[19], Y[19], A[18], B[18], Y[18]
  // _74157 74157_6: pin names not known; wires that end beside it: S, A[20], B[20], Y[20], A[21], B[21], Y[21], 1'b0, A[23], B[23], Y[23], A[22], B[22], Y[22]
  // _74157 74157_7: pin names not known; wires that end beside it: S, A[24], B[24], Y[24], A[25], B[25], Y[25], 1'b0, A[27], B[27], Y[27], A[26], B[26], Y[26]
endmodule

module _32_Bit_Mux (
  input  [31:0] B,
  input  [31:0] A,
  input  S,
  output [31:0] Y
);

  // _74157 74157_1: pin names not known; wires that end beside it: S, A[0], B[0], Y[0], A[1], B[1], Y[1], 1'b0, A[3], B[3], Y[3], A[2], B[2], Y[2]
  _28_Bit_Mux _28_Mux (.B(B[31:4]), .A(A[31:4]), .S(S), .Y(Y[31:4]));

  // Other names for the same wires on the sheet: A_4__28[27:0] = A[31:4]; B_4__28[27:0] = B[31:4];
  //   Y_4__28[27:0] = Y[31:4]
endmodule

module Rearrange2 (
  input  [8:0] Expo_A,
  input  [8:0] Expo_B,
  input  [31:0] A,
  input  [31:0] B,
  output [31:0] larger,
  output [31:0] smaller
);

  wire Borrow;

  Subtractor #(.width(9)) subtractor_1 (.a(Expo_A), .b(Expo_B), .bin(1'b0), .bout(Borrow));  // open: out
  _32_Bit_Mux u_32_bit_mux_1 (.B(B), .A(A), .S(Borrow), .Y(larger));
  _32_Bit_Mux u_32_bit_mux_2 (.B(A), .A(B), .S(Borrow), .Y(smaller));
endmodule

module Check_If_Zero (
  input  [31:0] X,
  output Zero_or_One
);

  wire n7432_1_p3, n7432_1_p6, n7432_1_p9, n7432_1_p12, n7432_2_p3, n7432_2_p6, n7432_2_p9, n7432_2_p12,
       n7432_3_p3, n7432_3_p6, n7432_3_p9, n7432_3_p12, n7432_4_p3, n7432_4_p6, n7432_4_p9, n7432_4_p12,
       n7432_5_p3, n7432_5_p6, n7432_5_p9, n7432_5_p12, n7432_6_p3, n7432_6_p6, n7432_6_p9, n7432_6_p12,
       n7432_7_p3, n7432_7_p6, n7432_7_p9, n7432_7_p12, n7432_8_p3, n7432_8_p6;

  // _7432 7432_1: pin names not known; wires that end beside it: X[0], X[1], n7432_1_p3, n7432_1_p3, X[2], n7432_1_p6, X[3], X[4], n7432_1_p9, n7432_1_p9, n7432_1_p6, n7432_1_p12
  // _7432 7432_2: pin names not known; wires that end beside it: X[20], X[21], n7432_2_p3, n7432_2_p3, X[22], n7432_2_p6, X[23], X[24], n7432_2_p9, n7432_2_p9, n7432_2_p6, n7432_2_p12
  // _7432 7432_3: pin names not known; wires that end beside it: X[5], X[6], n7432_3_p3, n7432_3_p3, X[7], n7432_3_p6, X[8], X[9], n7432_3_p9, n7432_3_p9, n7432_3_p6, n7432_3_p12
  // _7432 7432_4: pin names not known; wires that end beside it: X[25], X[26], n7432_4_p3, n7432_4_p3, X[27], n7432_4_p6, X[28], X[29], n7432_4_p9, n7432_4_p9, n7432_4_p6, n7432_4_p12
  // _7432 7432_5: pin names not known; wires that end beside it: X[10], X[11], n7432_5_p3, n7432_5_p3, X[12], n7432_5_p6, X[13], X[14], n7432_5_p9, n7432_5_p9, n7432_5_p6, n7432_5_p12
  // _7432 7432_6: pin names not known; wires that end beside it: X[30], 1'b0, n7432_6_p3, n7432_6_p3, n7432_4_p12, n7432_6_p6, n7432_1_p12, n7432_2_p12, n7432_6_p9, n7432_6_p9, n7432_6_p6, n7432_6_p12
  // _7432 7432_7: pin names not known; wires that end beside it: X[15], X[16], n7432_7_p3, n7432_7_p3, X[17], n7432_7_p6, X[18], X[19], n7432_7_p9, n7432_7_p9, n7432_7_p6, n7432_7_p12
  // _7432 7432_8: pin names not known; wires that end beside it: n7432_7_p12, n7432_5_p12, n7432_8_p3, n7432_8_p3, n7432_3_p12, n7432_8_p6, n7432_6_p12, n7432_8_p6, Zero_or_One
endmodule

module Shift_wrapper (
  input  [25:0] Padded_Number,
  input  [8:0] Expo_difference,
  output [25:0] Shifted_Num_2
);

  wire [4:0] RSA_e;

  Right_Shift_Adapter RSA (.S(Expo_difference), .E(RSA_e));
  Right_Shifter Right_Shifter (.E(RSA_e), .Padded_Number(Padded_Number), .Shifted_Number(Shifted_Num_2));
endmodule

module Right_Shift_Adapter (
  input  [8:0] S,
  output [4:0] E
);

  wire n7432_1_p2;

  // Probe on S
  // _7432 7432_1: pin names not known; wires that end beside it: S[4], n7432_1_p2, E[4], S[3], n7432_1_p2, E[3], n7432_1_p2, S[1], E[1], n7432_1_p2, S[2], E[2]
  Subtractor #(.width(9)) subtractor_1 (.a(9'h1a), .b(S), .bin(1'b0), .bout(n7432_1_p2));  // open: out
  // _7432 7432_2: pin names not known; wires that end beside it: S[0], n7432_1_p2, E[0], n7432_1_p2, n7432_1_p2, n7432_1_p2
endmodule

module Right_Shifter (
  input  [4:0] E,
  input  [25:0] Padded_Number,
  output [25:0] Shifted_Number
);

  wire [25:0] _2RS__2_bit_shifted_or_not, _4RS__4_bit_shifted_or_not, _8RS__8_bit_shifted_or_not,
       _16RS__4_bit_shifted_or_not;

  _16Bit_Right_Shifter _16RS (
    .in_1(Padded_Number), .Enable(E[4]), ._4_Bit_Shifted_or_not(_16RS__4_bit_shifted_or_not));  // open: _4Bit_RightShifted
  _8Bit_Right_Shifter _8RS (
    .in_1(_16RS__4_bit_shifted_or_not), .Enable(E[3]), ._8_Bit_Shifted_or_not(_8RS__8_bit_shifted_or_not));  // open: _8Bit_RightShifted
  _4Bit_Right_Shifter _4RS (
    .in_1(_8RS__8_bit_shifted_or_not), .Enable(E[2]), ._4_Bit_Shifted_or_not(_4RS__4_bit_shifted_or_not));  // open: _4Bit_RightShifted
  _2Bit_Right_Shifter _2RS (
    .in_1(_4RS__4_bit_shifted_or_not), .Enable(E[1]), ._2_Bit_Shifted_or_not(_2RS__2_bit_shifted_or_not));  // open: _2Bit_RightShifted
  _1Bit_Right_Shifter _1RS (
    .in_1(_2RS__2_bit_shifted_or_not), .Enable(E[0]), ._1_Bit_Shifted_or_not(Shifted_Number));  // open: _1Bit_RightShifted
endmodule

module Rounder (
  input  [24:0] Input,
  input  [8:0] Exponent,
  output [21:0] Rounded_Fraction,
  output [8:0] Rounded_Exponent,
  output Exponent_Overflow_While_Rounding
);

  wire adder_1_cout, AND_out, OR_out;
  wire [8:0] bit_extender_2_out;
  wire [9:9] adder_2_cout;
  wire [21:0] bit_extender_1_out;

  Bit_Extender #(.in_width(22), .out_width(22)) bit_extender_1 (.in({22{1'b0}}), .out(bit_extender_1_out));
  or OR (OR_out, Input[1], Input[0], Input[3]);
  and AND (AND_out, OR_out, Input[2]);
  Adder #(.width(22)) adder_1 (
    .a(Input[24:3]), .b(bit_extender_1_out), .out(Rounded_Fraction), .cin(AND_out), .cout(adder_1_cout));
  Bit_Extender #(.in_width(9), .out_width(9)) bit_extender_2 (.in({9{1'b0}}), .out(bit_extender_2_out));
  Adder #(.width(9)) adder_2 (
    .a(Exponent), .b(bit_extender_2_out), .out(Rounded_Exponent), .cin(adder_1_cout), .cout(adder_2_cout[9]));
  Subtractor #(.width(10)) subtractor_1 (
    .a(10'h1fe), .b({adder_2_cout[9], Rounded_Exponent}), .bout(Exponent_Overflow_While_Rounding));  // open: out, bin

  // Other names for the same wires on the sheet: Sticky = Input[0]; Round = Input[1]; Guard = Input[2];
  //   S[21:0] = Input[24:3]; S0 = Input[3]
endmodule

module FloatingPointAdder (
  input  [31:0] A,
  input  [31:0] B,
  output [31:0] Y,
  output Overflow,
  output Underflow,
  output INF,
  output NAN,
  output Denormalized_Number
);

  main main_1 (
    .A(A), .B(B), .Y(Y), .out_4(Overflow), .out_5(Underflow), .Infinity(INF), .Not_a_Number(NAN),
    .Denormalized_Number(Denormalized_Number));
endmodule

module flags (
  input  [8:0] Normal_Exponent,
  input  [24:0] Normal_Fraction,
  output INF,
  output NAN,
  output Denormalized_Number
);

  wire Exponent_all_0, Exponent_all_1, Fraction_all_0, not_3_out, or_1_out, or_2_out;

  and and_1 (Exponent_all_1, Normal_Exponent[0], Normal_Exponent[1], Normal_Exponent[2], Normal_Exponent[3], Normal_Exponent[4], Normal_Exponent[5], Normal_Exponent[6], Normal_Exponent[7], Normal_Exponent[8]);
  and and_2 (INF, Exponent_all_1, Fraction_all_0);
  and and_3 (NAN, Exponent_all_1, not_3_out);
  or or_1 (or_1_out, Normal_Exponent[0], Normal_Exponent[1], Normal_Exponent[2], Normal_Exponent[3], Normal_Exponent[4], Normal_Exponent[5], Normal_Exponent[6], Normal_Exponent[7], Normal_Exponent[8]);
  not not_1 (Exponent_all_0, or_1_out);
  and and_4 (Denormalized_Number, not_3_out, Exponent_all_0);
  not not_2 (Fraction_all_0, or_2_out);
  or or_2 (or_2_out, Normal_Fraction[0], Normal_Fraction[1], Normal_Fraction[2], Normal_Fraction[3], Normal_Fraction[4], Normal_Fraction[5], Normal_Fraction[6], Normal_Fraction[7], Normal_Fraction[8], Normal_Fraction[9], Normal_Fraction[10], Normal_Fraction[11], Normal_Fraction[12], Normal_Fraction[13], Normal_Fraction[14], Normal_Fraction[15], Normal_Fraction[16], Normal_Fraction[17], Normal_Fraction[18], Normal_Fraction[19], Normal_Fraction[20], Normal_Fraction[21], Normal_Fraction[22], Normal_Fraction[23], Normal_Fraction[24]);
  not not_3 (not_3_out, Fraction_all_0);

  // Other names for the same wires on the sheet: E[8:0] = Normal_Exponent; F[24:0] = Normal_Fraction
endmodule
