// Logisim project normalizer.circ as structural Verilog: 18 circuits, main circuit main
module main (
  input  [26:0] Significand,
  input  [8:0] Exponent,
  output [24:0] Normal_Significand,
  output [8:0] Normal_Exponent,
  output Overflow,
  output Underflow
);

  normalizer normalizer (
    .significand(Significand), .Exponent(Exponent), .Normal_Fraction(Normal_Significand),
    .Normal_Exponent(Normal_Exponent), .Overflow(Overflow), .Underflow(Underflow));
endmodule

module _16_bit_encoder (
  input  [15:0] I,
  input  EI,
  output [3:0] O,
  output EO,
  output GS
);

  wire A0_0, A0_1, A1_0, A1_1, A2_0, A2_1, GS_0, n74148_1__15__eo;

  _74148 u_74148_1 (
    ._1__I4(I[12]), ._2__I5(I[13]), ._3__I6(I[14]), ._4__I7(I[15]), ._5__EI(EI), ._6__A2(A2_1),
    ._7__A1(A1_1), ._15__EO(n74148_1__15__eo), ._16__GS(O[3]), ._13__I3(I[11]), ._12__I2(I[10]),
    ._11__I1(I[9]), ._10__I0(I[8]), ._9__A0(A0_1));  // open: _8__GND, _16__Vcc
  _74148 u_74148_2 (
    ._1__I4(I[4]), ._2__I5(I[5]), ._3__I6(I[6]), ._4__I7(I[7]), ._5__EI(n74148_1__15__eo), ._6__A2(A2_0),
    ._7__A1(A1_0), ._15__EO(EO), ._16__GS(GS_0), ._13__I3(I[3]), ._12__I2(I[2]), ._11__I1(I[1]),
    ._10__I0(I[0]), ._9__A0(A0_0));  // open: _8__GND, _16__Vcc
  // _7408 7408_1: pin names not known; wires that end beside it: A2_1, A2_0, O[2], A1_1, A1_0, O[1], A0_1, A0_0, O[0], GS_0, O[3], GS

  // Other names for the same wires on the sheet: A0 = O[0]; A1 = O[1]; A2 = O[2]; A3 = O[3]
endmodule

module _74148 (
  input  _1__I4,
  input  _16__Vcc,
  input  _2__I5,
  input  _3__I6,
  input  _4__I7,
  input  _13__I3,
  input  _5__EI,
  input  _12__I2,
  input  _11__I1,
  input  _10__I0,
  input  _8__GND,
  output _15__EO,
  output _16__GS,
  output _6__A2,
  output _7__A1,
  output _9__A0
);

  wire not_1_out, not_2_out, not_3_out, not_4_out, not_5_out, not_6_out, not_7_out, not_8_out, not_9_out,
       not_10_out, not_11_out, not_12_out, priority_encoder_1_en_out, priority_encoder_1_gs;
  wire [2:0] priority_encoder_1_out;

  or or_1 (_16__GS, priority_encoder_1_en_out, _5__EI);
  not not_1 (not_1_out, _10__I0);
  not not_2 (not_2_out, _11__I1);
  not not_3 (not_3_out, _12__I2);
  not not_4 (not_4_out, _13__I3);
  Priority_Encoder #(.disabled(0)) priority_encoder_1 (
    .in0(not_1_out), .in1(not_2_out), .in2(not_3_out), .in3(not_4_out), .in4(not_5_out), .in5(not_6_out),
    .in6(not_7_out), .in7(not_8_out), .out(priority_encoder_1_out), .en_in(not_9_out),
    .gs(priority_encoder_1_gs), .en_out(priority_encoder_1_en_out));
  not not_5 (not_5_out, _1__I4);
  not not_6 (not_6_out, _2__I5);
  not not_7 (not_7_out, _3__I6);
  not not_8 (not_8_out, _4__I7);
  not not_9 (not_9_out, _5__EI);
  or or_2 (_15__EO, priority_encoder_1_gs, _5__EI);
  not not_10 (not_10_out, priority_encoder_1_out[0]);
  not not_11 (not_11_out, priority_encoder_1_out[1]);
  not not_12 (not_12_out, priority_encoder_1_out[2]);
  or or_3 (_9__A0, not_10_out, _16__GS);
  or or_4 (_7__A1, not_11_out, _16__GS);
  or or_5 (_6__A2, not_12_out, _16__GS);

  // Other names for the same wires on the sheet: A0 = _9__A0; A1 = _7__A1; A2 = _6__A2; E = _5__EI; EO = _15__EO;
  //   GS = _16__GS; I0 = _10__I0; I1 = _11__I1; I2 = _12__I2; I3 = _13__I3; I4 = _1__I4; I5 = _2__I5; I6 = _3__I6;
  //   I7 = _4__I7

  // Notes on the sheet:
  //   _16__Vcc: pull=up
  //   _8__GND: pull=down
  //   74148: 8-Line to 4-Line Priority Encoder
endmodule

module _32_bit_encoder (
  input  EI,
  input  [31:0] I,
  output [4:0] O
);

  wire _16_bit_encoder_eo, O0_0, O0_1, O1_0, O1_1, O2_0, O2_1, O3_0, O3_1;

  _16_bit_encoder _16_bit_encoder (
    .I(I[31:16]), .EI(EI), .O({O3_1, O2_1, O1_1, O0_1}), .EO(_16_bit_encoder_eo), .GS(O[4]));
  _16_bit_encoder _16_bit_encoder_2 (
    .I(I[15:0]), .EI(_16_bit_encoder_eo), .O({O3_0, O2_0, O1_0, O0_0}));  // open: EO, GS
  // _7408 7408_1: pin names not known; wires that end beside it: O2_1, O2_0, O[2], O1_1, O1_0, O[1], O0_1, O0_0, O[0], O3_1, O3_0, O[3]

  // Other names for the same wires on the sheet: I0[15:0] = I[15:0]; I1[15:0] = I[31:16];
  //   O_0[3:0] = {O3_0, O2_0, O1_0, O0_0}; O_1[3:0] = {O3_1, O2_1, O1_1, O0_1}
endmodule

module _32_bit_active_high_encoder (
  input  [31:0] I,
  input  _1_based_indexing,
  output [5:0] O
);

  wire I0_prime, I1_prime, I2_prime, I3_prime, I4_prime, I5_prime, I6_prime, I7_prime, I8_prime, I9_prime,
       I10_prime, I11_prime, I12_prime, I13_prime, I14_prime, I15_prime, I16_prime, I17_prime, I18_prime,
       I19_prime, I20_prime, I21_prime, I22_prime, I23_prime, I24_prime, I25_prime, I26_prime, I27_prime,
       I28_prime, I29_prime, I30_prime, I31_prime;
  wire [4:0] _32_bit_encoder_o, bit_extender_1_out;

  // _7404 7404_1: pin names not known; wires that end beside it: I[0], I0_prime, I[1], I1_prime, I[2], I2_prime, I[3], I3_prime, I[4], I4_prime, I[5], I5_prime
  // _7404 7404_2: pin names not known; wires that end beside it: I[6], I6_prime, I[7], I7_prime, I[8], I8_prime, I[9], I9_prime, I[10], I10_prime, I[11], I11_prime
  // _7404 7404_3: pin names not known; wires that end beside it: I[12], I12_prime, I[13], I13_prime, I[14], I14_prime, I[15], I15_prime, I[16], I16_prime, I[17], I17_prime
  // _7404 7404_4: pin names not known; wires that end beside it: I[18], I18_prime, I[19], I19_prime, I[20], I20_prime, I[21], I21_prime, I[22], I22_prime, I[23], I23_prime
  // _7404 7404_5: pin names not known; wires that end beside it: I[24], I24_prime, I[25], I25_prime, I[26], I26_prime, I[27], I27_prime, I[28], I28_prime, I[29], I29_prime
  // _7404 7404_6: pin names not known; wires that end beside it: I[30], I30_prime, I[31], I31_prime
  _32_bit_encoder _32_bit_encoder (
    .EI(1'b0),
    .I({I31_prime, I30_prime, I29_prime, I28_prime, I27_prime, I26_prime, I25_prime, I24_prime, I23_prime, I22_prime, I21_prime, I20_prime, I19_prime, I18_prime, I17_prime, I16_prime, I15_prime, I14_prime, I13_prime, I12_prime, I11_prime, I10_prime, I9_prime, I8_prime, I7_prime, I6_prime, I5_prime, I4_prime, I3_prime, I2_prime, I1_prime, I0_prime}),
    .O(_32_bit_encoder_o));
  assign bit_extender_1_out = {{4{1'b0}}, 1'b0};  // Bit_Extender bit_extender_1
  Adder #(.width(5)) adder_1 (
    .a(_32_bit_encoder_o), .b(bit_extender_1_out), .out(O[4:0]), .cin(_1_based_indexing), .cout(O[5]));

  // Other names for the same wires on the sheet: I_prime[31:0] = {I31_prime, I30_prime, I29_prime, I28_prime, I27_prime, I26_prime, I25_prime, I24_prime, I23_prime, I22_prime, I21_prime, I20_prime, I19_prime, I18_prime, I17_prime, I16_prime, I15_prime, I14_prime, I13_prime, I12_prime, I11_prime, I10_prime, I9_prime, I8_prime, I7_prime, I6_prime, I5_prime, I4_prime, I3_prime, I2_prime, I1_prime, I0_prime}
endmodule

module _28_bit_mux (
  input  [27:0] B,
  input  [27:0] A,
  input  S,
  output [27:0] Y
);

  // _74157 74157_1: pin names not known; wires that end beside it: S, A[0], B[0], Y[0], A[1], B[1], Y[1], 1'b0, A[3], B[3], Y[3], A[2], B[2], Y[2]
  // _74157 74157_2: pin names not known; wires that end beside it: S, A[4], B[4], Y[4], A[5], B[5], Y[5], 1'b0, A[7], B[7], Y[7], A[6], B[6], Y[6]
  // _74157 74157_3: pin names not known; wires that end beside it: S, A[8], B[8], Y[8], A[9], B[9], Y[9], 1'b0, A[11], B[11], Y[11], A[10], B[10], Y[10]
  // _74157 74157_4: pin names not known; wires that end beside it: S, A[12], B[12], Y[12], A[13], B[13], Y[13], 1'b0, A[15], B[15], Y[15], A[14], B[14], Y[14]
  // _74157 74157_5: pin names not known; wires that end beside it: S, A[16], B[16], Y[16], A[17], B[17], Y[17], 1'b0, A[19], B[19], Y[19], A[18], B[18], Y[18]
  // _74157 74157_6: pin names not known; wires that end beside it: S, A[20], B[20], Y[20], A[21], B[21], Y[21], 1'b0, A[23], B[23], Y[23], A[22], B[22], Y[22]
  // _74157 74157_7: pin names not known; wires that end beside it: S, A[24], B[24], Y[24], A[25], B[25], Y[25], 1'b0, A[27], B[27], Y[27], A[26], B[26], Y[26]
endmodule

module _1_bit_rs (
  input  [26:0] S,
  input  Enable,
  output [26:0] out_3
);

  wire [26:0] Shifted;
  wire [27:0] bit_extender_1_out, bit_extender_2_out;
  wire [27:27] _28_bit_mux_y;

  assign bit_extender_1_out = {{1{1'b0}}, Shifted};  // Bit_Extender bit_extender_1
  assign bit_extender_2_out = {{1{1'b0}}, S};  // Bit_Extender bit_extender_2
  Shifter #(.width(27), .shift("lr")) shifter_1 (.in(S), .\dist (5'b00001), .out(Shifted));
  _28_bit_mux _28_bit_mux (.B(bit_extender_1_out), .Y({_28_bit_mux_y[27], out_3}), .A(bit_extender_2_out), .S(Enable));
endmodule

module _1_bit_ls (
  input  [26:0] S,
  input  Enable,
  output [26:0] out_3
);

  wire [26:0] Shifted;
  wire [27:0] bit_extender_1_out, bit_extender_2_out;
  wire [27:27] _28_bit_mux_y;

  assign bit_extender_1_out = {{1{1'b0}}, Shifted};  // Bit_Extender bit_extender_1
  assign bit_extender_2_out = {{1{1'b0}}, S};  // Bit_Extender bit_extender_2
  Shifter #(.width(27)) shifter_1 (.in(S), .\dist (5'b00001), .out(Shifted));
  _28_bit_mux _28_bit_mux (.B(bit_extender_1_out), .Y({_28_bit_mux_y[27], out_3}), .A(bit_extender_2_out), .S(Enable));
endmodule

module _2_bit_ls (
  input  [26:0] S,
  input  Enable,
  output [26:0] out_3
);

  wire [26:0] Shifted;
  wire [27:0] bit_extender_1_out, bit_extender_2_out;
  wire [27:27] _28_bit_mux_y;

  assign bit_extender_1_out = {{1{1'b0}}, Shifted};  // Bit_Extender bit_extender_1
  assign bit_extender_2_out = {{1{1'b0}}, S};  // Bit_Extender bit_extender_2
  Shifter #(.width(27)) shifter_1 (.in(S), .\dist (5'b00010), .out(Shifted));
  _28_bit_mux _28_bit_mux (.B(bit_extender_1_out), .Y({_28_bit_mux_y[27], out_3}), .A(bit_extender_2_out), .S(Enable));
endmodule

module _4_bit_ls (
  input  [26:0] S,
  input  Enable,
  output [26:0] out_3
);

  wire [26:0] Shifted;
  wire [27:0] bit_extender_1_out, bit_extender_2_out;
  wire [27:27] _28_bit_mux_y;

  assign bit_extender_1_out = {{1{1'b0}}, Shifted};  // Bit_Extender bit_extender_1
  assign bit_extender_2_out = {{1{1'b0}}, S};  // Bit_Extender bit_extender_2
  Shifter #(.width(27)) shifter_1 (.in(S), .\dist (5'b00100), .out(Shifted));
  _28_bit_mux _28_bit_mux (.B(bit_extender_1_out), .Y({_28_bit_mux_y[27], out_3}), .A(bit_extender_2_out), .S(Enable));
endmodule

module _8_bit_ls (
  input  [26:0] S,
  input  Enable,
  output [26:0] out_3
);

  wire [26:0] Shifted;
  wire [27:0] bit_extender_1_out, bit_extender_2_out;
  wire [27:27] _28_bit_mux_y;

  assign bit_extender_1_out = {{1{1'b0}}, Shifted};  // Bit_Extender bit_extender_1
  assign bit_extender_2_out = {{1{1'b0}}, S};  // Bit_Extender bit_extender_2
  Shifter #(.width(27)) shifter_1 (.in(S), .\dist (5'b01000), .out(Shifted));
  _28_bit_mux _28_bit_mux (.B(bit_extender_1_out), .Y({_28_bit_mux_y[27], out_3}), .A(bit_extender_2_out), .S(Enable));
endmodule

module _16_bit_l_s (
  input  [26:0] S,
  input  Enable,
  output [26:0] out_3
);

  wire [26:0] Shifted;
  wire [27:0] bit_extender_1_out, bit_extender_2_out;
  wire [27:27] _28_bit_mux_y;

  assign bit_extender_1_out = {{1{1'b0}}, Shifted};  // Bit_Extender bit_extender_1
  assign bit_extender_2_out = {{1{1'b0}}, S};  // Bit_Extender bit_extender_2
  Shifter #(.width(27)) shifter_1 (.in(S), .\dist (5'b10000), .out(Shifted));
  _28_bit_mux _28_bit_mux (.B(bit_extender_1_out), .Y({_28_bit_mux_y[27], out_3}), .A(bit_extender_2_out), .S(Enable));
endmodule

module left_shifter (
  input  [4:0] E,
  input  [26:0] A,
  output [26:0] Y
);

  wire [26:0] _2_bit_ls_out_3, _4_bit_ls_out_3, _8_bit_ls_out_3, _16_bit_ls_out_3;

  _16_bit_l_s _16_bit_ls (.S(A), .Enable(E[4]), .out_3(_16_bit_ls_out_3));
  _8_bit_ls _8_bit_ls (.S(_16_bit_ls_out_3), .Enable(E[3]), .out_3(_8_bit_ls_out_3));
  _4_bit_ls _4_bit_ls (.S(_8_bit_ls_out_3), .Enable(E[2]), .out_3(_4_bit_ls_out_3));
  _2_bit_ls _2_bit_ls (.S(_4_bit_ls_out_3), .Enable(E[1]), .out_3(_2_bit_ls_out_3));
  _1_bit_ls _1_bit_ls (.S(_2_bit_ls_out_3), .Enable(E[0]), .out_3(Y));
endmodule

module _5_bit_mux (
  input  [4:0] B,
  input  [4:0] A,
  input  S,
  output [4:0] Y
);

  // _74157 74157_1: pin names not known; wires that end beside it: S, A[0], B[0], Y[0], A[1], B[1], Y[1], 1'b0, A[3], B[3], Y[3], A[2], B[2], Y[2]
  // _74157 74157_2: pin names not known; wires that end beside it: S, A[4], B[4], Y[4], 1'b0
endmodule

module asu (
  input  B_Cin,
  input  Add,
  input  [24:0] A,
  input  [24:0] B,
  output [25:0] Y
);

  wire bout, cout;
  wire [24:0] Add_t, Sub;

  // Probe on B
  // Probe on A
  Adder #(.width(25)) adder_1 (.a(A), .b(B), .out(Add_t), .cin(B_Cin), .cout(cout));
  Subtractor #(.width(25)) subtractor_1 (.a(A), .b(B), .out(Sub), .bin(B_Cin), .bout(bout));
  // _74157 74157_1: pin names not known; wires that end beside it: Add, bout, cout, Y[25], 1'b0
  Multiplexer #(.width(25), .enable("false")) multiplexer_1 (.in0(Sub), .in1(Add_t), .out(Y[24:0]), .sel(Add));
  // Probe on Y
endmodule

module _9_bit_mux (
  input  [8:0] B,
  input  [8:0] A,
  input  S,
  output [8:0] Y
);

  // _74157 74157_1: pin names not known; wires that end beside it: S, A[0], B[0], Y[0], A[1], B[1], Y[1], 1'b0, A[3], B[3], Y[3], A[2], B[2], Y[2]
  // _74157 74157_2: pin names not known; wires that end beside it: S, A[4], B[4], Y[4], A[5], B[5], Y[5], 1'b0, A[7], B[7], Y[7], A[6], B[6], Y[6]
  // _74157 74157_3: pin names not known; wires that end beside it: S, A[8], B[8], Y[8], 1'b0
endmodule

module error_detector (
  input  [8:0] Exponent,
  input  Carry_borrow,
  output Overflow_Underflow
);

  Subtractor #(.width(10)) subtractor_1 (
    .a(10'h1fe), .b({Carry_borrow, Exponent}), .bout(Overflow_Underflow));  // open: out, bin
endmodule

module normalizer (
  input  [26:0] significand,
  input  [8:0] Exponent,
  output [24:0] Normal_Fraction,
  output [8:0] Normal_Exponent,
  output Overflow,
  output Underflow
);

  wire Add, Carry, E0, E1, E2, E3, E4, E9, n7402_1_p1, n7432_2_p3, n7432_2_p6, n7432_2_p8, n7432_2_p9,
       n7432_3_p3, n7432_3_p6, Overflow_underflow, Sub;
  wire [4:0] _5_bit_mux_y, bit_extender_1_out, left_shift_amount;
  wire [5:5] _32_bit_active_high_encoder_o;
  wire [8:0] ModifiedExponent;
  wire [24:0] bit_extender_2_out, bit_extender_3_out;
  wire [25:10] asu_y;
  wire [26:0] _1_bit_rs_out_3;
  wire [26:25] left_shifter_y;

  // _7432 7432_1: pin names not known; wires that end beside it: significand[25], significand[26], Add
  // _7432 7432_2: pin names not known; wires that end beside it: significand[26], left_shift_amount[0], n7432_2_p3, n7432_2_p3, left_shift_amount[1], n7432_2_p6, left_shift_amount[2], n7432_2_p8, n7432_2_p9, left_shift_amount[3], n7432_2_p6, n7432_2_p8
  // _7404 7404_1: pin names not known; wires that end beside it: Add, Sub
  _1_bit_rs _1_bit_rs (.S(significand), .Enable(significand[26]), .out_3(_1_bit_rs_out_3));
  assign bit_extender_1_out = {{4{1'b0}}, significand[26]};  // Bit_Extender bit_extender_1
  // _7432 7432_3: pin names not known; wires that end beside it: left_shift_amount[4], n7432_2_p9, n7432_3_p3, n7432_3_p3, significand[25], n7432_3_p6
  left_shifter left_shifter (.A(_1_bit_rs_out_3), .E({E4, E3, E2, E1, E0}), .Y({left_shifter_y, Normal_Fraction}));
  _5_bit_mux _5_bit_mux (.Y(_5_bit_mux_y), .B(bit_extender_1_out), .A(left_shift_amount), .S(Add));
  // _7408 7408_1: pin names not known; wires that end beside it: n7432_3_p6, E9, Carry, Add, Overflow_underflow, Overflow, Overflow_underflow, Sub, Underflow
  _32_bit_active_high_encoder _32_bit_active_high_encoder (
    .I({significand[24:0], {7{1'b0}}}), ._1_based_indexing(1'b1),
    .O({_32_bit_active_high_encoder_o[5], left_shift_amount}));
  assign bit_extender_2_out = {{20{1'b0}}, _5_bit_mux_y};  // Bit_Extender bit_extender_2
  _9_bit_mux _9_bit_mux (.B(ModifiedExponent), .Y(Normal_Exponent), .A({9{1'b0}}), .S(n7432_3_p6));
  // _7402 7402_1: pin names not known; wires that end beside it: n7402_1_p1, significand[25], significand[26]
  assign bit_extender_3_out = {{16{1'b0}}, Exponent};  // Bit_Extender bit_extender_3
  // _7408 7408_2: pin names not known; wires that end beside it: n7402_1_p1, left_shift_amount[4], E4, n7402_1_p1, left_shift_amount[3], E3, n7402_1_p1, left_shift_amount[2], E2, n7402_1_p1, left_shift_amount[1], E1
  asu asu (.B_Cin(1'b0), .A(bit_extender_3_out), .B(bit_extender_2_out), .Add(Add), .Y({asu_y, E9, ModifiedExponent}));
  error_detector error_detector (
    .Exponent(Normal_Exponent), .Carry_borrow(Carry), .Overflow_Underflow(Overflow_underflow));
  // _7408 7408_3: pin names not known; wires that end beside it: n7402_1_p1, left_shift_amount[0], E0

  // Other names for the same wires on the sheet: O0 = left_shift_amount[0]; O1 = left_shift_amount[1];
  //   O2 = left_shift_amount[2]; O3 = left_shift_amount[3]; O4 = left_shift_amount[4]; S25 = significand[25];
  //   S26 = significand[26]
endmodule
