// Logisim project rounder.circ as structural Verilog: 1 circuit, main circuit Rounder
module Rounder (
  input  [24:0] Input,
  input  [8:0] Exponent,
  output [21:0] Rounded_Fraction,
  output [8:0] Rounded_Exponent,
  output Exponent_Overflow_While_Rounding
);

  wire adder_1_cout, AND_out, OR_out;
  wire [8:0] bit_extender_2_out;
  wire [9:9] adder_2_cout;
  wire [21:0] bit_extender_1_out;

  Bit_Extender #(.in_width(22), .out_width(22)) bit_extender_1 (.in({22{1'b0}}), .out(bit_extender_1_out));
  or OR (OR_out, Input[1], Input[0], Input[3]);
  and AND (AND_out, OR_out, Input[2]);
  Adder #(.width(22)) adder_1 (
    .a(Input[24:3]), .b(bit_extender_1_out), .out(Rounded_Fraction), .cin(AND_out), .cout(adder_1_cout));
  Bit_Extender #(.in_width(9), .out_width(9)) bit_extender_2 (.in({9{1'b0}}), .out(bit_extender_2_out));
  Adder #(.width(9)) adder_2 (
    .a(Exponent), .b(bit_extender_2_out), .out(Rounded_Exponent), .cin(adder_1_cout), .cout(adder_2_cout[9]));
  Subtractor #(.width(10)) subtractor_1 (
    .a(10'h1fe), .b({adder_2_cout[9], Rounded_Exponent}), .bout(Exponent_Overflow_While_Rounding));  // open: out, bin

  // Other names for the same wires on the sheet: Sticky = Input[0]; Round = Input[1]; Guard = Input[2];
  //   S[21:0] = Input[24:3]; S0 = Input[3]
endmodule
